// Logisim project alu.circ as structural Verilog: 1 circuit, main circuit alu
module alu (
  input  [31:0] A,
  input  [31:0] B,
  input  [3:0] ALUSel,
  output [31:0] Result
);

  wire xor_2_out;
  wire [0:0] result13;
  wire [5:0] bitadder_1_out, bitadder_2_out, result15;
  wire [31:0] divider_2_out, multiplexer_2_out, multiplexer_3_out, multiplier_2_out, multiplier_3_out,
       multiplier_4_cout, multiplier_5_cout, negator_1_out, negator_2_out, negator_3_out, negator_4_out,
       negator_5_out, result0, result1, result2, result3, result4, result5, result6, result7, result8,
       result9, result10, result11, result12, result14;

  Shifter #(.width(32), .shift("lr")) shifter_1 (.in(A), .\dist (B[4:0]), .out(result11));
  Shifter #(.width(32), .shift("ar")) shifter_2 (.in(A), .\dist (B[4:0]), .out(result12));
  Shifter #(.width(32)) shifter_3 (.in(A), .\dist (B[4:0]), .out(result14));
  Comparator #(.width(32)) comparator_1 (.a(A), .b(B), .lt(result13[0]));  // open: gt, eq
  BitAdder #(.width(32)) bitadder_1 (.in0(A), .out(bitadder_1_out));
  BitAdder #(.width(32)) bitadder_2 (.in0(B), .out(bitadder_2_out));
  Adder #(.width(6)) adder_1 (.a(bitadder_1_out), .b(bitadder_2_out), .out(result15));  // open: cin, cout
  assign result0 = A & B;  // AND_Gate and_1, 32 bits wide
  assign result1 = A | B;  // OR_Gate or_1, 32 bits wide
  Adder #(.width(32)) adder_2 (.a(A), .b(B), .out(result3));  // open: cin, cout
  Subtractor #(.width(32)) subtractor_1 (.a(A), .b(B), .out(result4));  // open: bin, bout
  Multiplier #(.width(32)) multiplier_1 (.a(A), .b(B), .out(result5), .cout(result6));  // open: cin
  assign result2 = A ^ B;  // XOR_Gate xor_1, 32 bits wide
  Multiplexer #(.select(4), .width(32), .enable("false")) multiplexer_1 (
    .in0(result0), .in1(result1), .in2(result2), .in3(result3), .in4(result4), .in5(result5), .in6(result6),
    .in7(result7), .in8(result8), .in9(result9), .in10(result10), .in11(result11), .in12(result12),
    .in13({{31{1'b0}}, result13[0]}), .in14(result14), .in15({{26{1'b0}}, result15}), .out(Result),
    .sel(ALUSel));
  Negator #(.width(32)) negator_1 (.in(A), .out(negator_1_out));
  Negator #(.width(32)) negator_2 (.in(B), .out(negator_2_out));
  Multiplexer #(.width(32), .enable("false")) multiplexer_2 (
    .in0(A), .in1(negator_1_out), .out(multiplexer_2_out), .sel(A[31]));
  Multiplexer #(.width(32), .enable("false")) multiplexer_3 (
    .in0(B), .in1(negator_2_out), .out(multiplexer_3_out), .sel(B[31]));
  xor xor_2 (xor_2_out, A[31], B[31]);
  Divider #(.width(32)) divider_1 (.a(A), .b(B), .out(result8), .rem(result10));  // open: upper
  Divider #(.width(32)) divider_2 (
    .a(multiplexer_2_out), .b(multiplexer_3_out), .out(divider_2_out));  // open: upper, rem
  Negator #(.width(32)) negator_3 (.in(divider_2_out), .out(negator_3_out));
  Multiplexer #(.width(32), .enable("false")) multiplexer_4 (
    .in0(divider_2_out), .in1(negator_3_out), .out(result9), .sel(xor_2_out));
  Multiplier #(.width(32)) multiplier_2 (
    .a(B), .b({32{1'b1}}), .out(multiplier_2_out), .cin(multiplier_4_cout));  // open: cout
  Multiplier #(.width(32)) multiplier_3 (
    .a(A), .b({32{1'b1}}), .out(multiplier_3_out), .cin(multiplier_4_cout));  // open: cout
  Negator #(.width(32)) negator_4 (.in(A), .out(negator_4_out));
  Negator #(.width(32)) negator_5 (.in(B), .out(negator_5_out));
  Multiplier #(.width(32)) multiplier_4 (.a(A), .b(B), .cout(multiplier_4_cout));  // open: out, cin
  Multiplier #(.width(32)) multiplier_5 (
    .a(negator_4_out), .b(negator_5_out), .cout(multiplier_5_cout));  // open: out, cin
  Multiplexer #(.select(2), .width(32), .enable("false")) multiplexer_5 (
    .in0(multiplier_4_cout), .in1(multiplier_2_out), .in2(multiplier_3_out), .in3(multiplier_5_cout),
    .out(result7), .sel({B[31], A[31]}));

  // Notes on the sheet:
  //   INPUTS to your circuit
  //   DON'T CHANGE THE LOCATIONS OF THE INPUTS AND OUTPUTS!
  //   OUTPUT from your circuit
endmodule
