// Logisim project cpu.circ as structural Verilog: 1 circuit, main circuit main
module main (
  input  [31:0] INSTRUCTION,
  input  CLOCK,
  output [31:0] FETCH_ADDRESS,
  output [31:0] ra,
  output [31:0] sp,
  output [31:0] t0,
  output [31:0] t1,
  output [31:0] t2,
  output [31:0] s0,
  output [31:0] s1,
  output [31:0] a0
);

  wire add_every, alu_result, and_1_out, and_4_out, and_5_out, and_6_out, and_8_out, and_17_out, and_18_out,
       and_27_out, and_28_out, and_31_out, and_37_out, and_38_out, and_41_out, and_42_out, and_43_out,
       and_45_out, and_48_out, and_49_out, and_50_out, and_51_out, and_52_out, and_55_out, and_andi, beq,
       bgeu, bitfinder_3_index, bitfinder_4_index, bitfinder_5_index, bitfinder_6_index, blt, bltu, bne,
       BrEq, Brlt, Brun, comparator_3_eq, comparator_4_eq, comparator_5_eq, comparator_6_eq, comparator_7_eq,
       comparator_8_eq, comparator_9_eq, comparator_10_eq, comparator_11_eq, comparator_12_eq,
       comparator_13_eq, comparator_14_eq, comparator_15_eq, comparator_16_eq, comparator_17_eq,
       comparator_18_eq, comparator_19_eq, comparator_20_eq, comparator_21_eq, comparator_22_eq,
       comparator_23_eq, comparator_24_eq, comparator_25_eq, comparator_26_eq, comparator_27_eq,
       comparator_28_eq, comparator_29_eq, comparator_30_eq, comparator_31_eq, comparator_32_eq,
       comparator_33_eq, comparator_34_eq, comparator_35_eq, comparator_36_eq, comparator_37_eq,
       comparator_38_eq, comparator_39_eq, comparator_40_eq, comparator_41_eq, comparator_42_eq,
       comparator_43_eq, comparator_44_eq, comparator_45_eq, comparator_46_eq, comparator_47_eq,
       comparator_48_eq, comparator_49_eq, comparator_50_eq, comparator_51_eq, comparator_52_eq,
       comparator_53_eq, comparator_54_eq, comparator_55_eq, comparator_56_eq, div, divu, I_3_13_67, I_13_01,
       i_simple_type, i_type_load, is_b_type, is_lb, is_lbu, is_lh, is_lhu, is_lw, jalr_jal, mem_rw, mul,
       mulh, mulhu, no_wb, not_1_out, not_2_out, not_3_out, not_4_out, not_5_out, not_6_out, not_7_out,
       not_8_out, not_9_out, not_10_out, not_11_out, not_12_out, not_13_out, not_14_out, not_15_out,
       not_16_out, not_17_out, not_18_out, not_19_out, not_20_out, not_21_out, not_22_out, not_23_out,
       not_24_out, not_25_out, not_26_out, not_27_out, not_28_out, not_29_out, not_30_out, not_31_out,
       not_32_out, not_33_out, not_34_out, not_35_out, not_36_out, not_37_out, not_38_out, not_39_out,
       not_40_out, not_41_out, not_43_out, not_44_out, not_45_out, not_46_out, not_48_out, not_49_out,
       not_50_out, not_51_out, not_54_out, not_55_out, not_56_out, not_57_out, not_58_out, not_59_out,
       not_60_out, not_61_out, not_62_out, not_63_out, not_64_out, not_65_out, op_src, or_4_out, or_7_out,
       or_ori, pc_sel, pc_src, pc_used, r_type, reg_we, remu, S_01000, s_type, SB_11000, signed_BrEq,
       signed_Brlt, sll_slli, slti, srl_srli, sub, U_0_101, u_type_auipc, u_type_lui, UJ_11011,
       unsigned_BrEq, unsigned_Brlt, xor_xori;
  wire [1:0] bitfinder_2_index, d_src;
  wire [1:1] not_42_out, not_47_out, not_52_out, not_53_out;
  wire [2:0] bitfinder_1_index, bitfinder_7_index, func3, imm_sel;
  wire [3:0] alu_sel, bitfinder_8_index;
  wire [6:6] func7;
  wire [7:7] lbu;
  wire [15:15] lhu;
  wire [19:0] instruc_after_reg;
  wire [31:0] adder_1_out, adder_2_out, byte1, byte2, byte3, byte4, halfword1, I_imm, IMM, lb, load_result,
       multiplexer_1_out, multiplexer_2_out, multiplexer_5_out, multiplexer_6_out, offset, PC_q,
       register_2_q, ubyte1, uhalfword2, write_back, x_rs1, x_rs2;
  wire [31:1] B_imm;
  wire [31:4] I_SHIFT_imm;
  wire [31:7] halfword2;
  wire [31:11] S_imm;
  wire [31:15] lh;
  wire [31:20] J_imm;
  wire [31:31] load_data;

  Adder #(.width(32)) adder_1 (.a(PC_q), .b(32'h4), .out(adder_1_out));  // open: cin, cout
  Multiplexer #(.width(32), .enable("false")) multiplexer_1 (
    .in0(adder_1_out), .in1(offset), .out(multiplexer_1_out), .sel(pc_sel));
  Register #(.width(32)) PC (.D(multiplexer_1_out), .clk(CLOCK), .Q(PC_q));  // open: en, clr
  Multiplexer #(.width(32), .enable("false")) multiplexer_2 (
    .in0(INSTRUCTION), .in1(32'h13), .out(multiplexer_2_out), .sel(pc_sel));
  not not_1 (not_1_out, func3[1]);
  Register #(.width(32)) register_1 (
    .D(multiplexer_2_out), .clk(CLOCK),
    .Q({func7[6], B_imm[10:5], I_imm[4:0], instruc_after_reg[19:15], func3, B_imm[4:1], B_imm[11], instruc_after_reg[6:0]}));  // open: en, clr
  not not_2 (not_2_out, instruc_after_reg[2]);
  not not_3 (not_3_out, instruc_after_reg[3]);
  not not_4 (not_4_out, instruc_after_reg[4]);
  not not_5 (not_5_out, instruc_after_reg[6]);
  not not_6 (not_6_out, instruc_after_reg[2]);
  not not_7 (not_7_out, instruc_after_reg[3]);
  not not_8 (not_8_out, instruc_after_reg[4]);
  not not_9 (not_9_out, instruc_after_reg[2]);
  not not_10 (not_10_out, instruc_after_reg[3]);
  not not_11 (not_11_out, instruc_after_reg[4]);
  not not_12 (not_12_out, instruc_after_reg[5]);
  not not_13 (not_13_out, instruc_after_reg[6]);
  not not_14 (not_14_out, instruc_after_reg[3]);
  not not_15 (not_15_out, instruc_after_reg[4]);
  not not_16 (not_16_out, instruc_after_reg[2]);
  not not_17 (not_17_out, instruc_after_reg[3]);
  not not_18 (not_18_out, instruc_after_reg[5]);
  not not_19 (not_19_out, instruc_after_reg[6]);
  and and_1 (and_1_out, func3[0], not_1_out);
  Register #(.width(32)) register_2 (.D(PC_q), .clk(CLOCK), .Q(register_2_q));  // open: en, clr
  Shifter #(.width(32), .shift("lr")) shifter_1 (.in(PC_q), .\dist (5'b00010), .out(FETCH_ADDRESS));
  and and_2 (S_01000, not_2_out, not_3_out, not_4_out, instruc_after_reg[5], not_5_out);
  and and_3 (SB_11000, not_6_out, not_7_out, not_8_out, instruc_after_reg[5], instruc_after_reg[6]);
  and and_4 (and_4_out, not_9_out, not_10_out, not_11_out, not_12_out, not_13_out);
  and and_5 (and_5_out, instruc_after_reg[2], not_14_out, not_15_out, instruc_after_reg[5], instruc_after_reg[6]);
  and and_6 (and_6_out, not_16_out, not_17_out, instruc_after_reg[4], not_18_out, not_19_out);
  not not_20 (not_20_out, and_1_out);
  and and_7 (I_13_01, and_6_out, and_1_out);
  Adder #(.width(32)) adder_2 (.a(register_2_q), .b(32'h4), .out(adder_2_out));  // open: cin, cout
  and and_8 (and_8_out, and_6_out, not_20_out);
  not not_21 (not_21_out, instruc_after_reg[3]);
  not not_22 (not_22_out, instruc_after_reg[6]);
  not not_23 (not_23_out, instruc_after_reg[4]);
  or or_1 (I_3_13_67, and_4_out, and_5_out, and_8_out);
  regfile_main RegFile (
    .Read_Register_1_rs1(instruc_after_reg[19:15]), .Read_Register_2_rs2(I_imm[4:0]),
    .Write_Register_rd({B_imm[4:1], B_imm[11]}), .Write_Data(write_back), .Write_Enable(reg_we),
    .Clock(CLOCK), .Read_Data_1(x_rs1), .Read_Data_2(x_rs2), .ra(ra), .sp(sp), .t0(t0), .t1(t1), .t2(t2),
    .s0(s0), .s1(s1), .a0(a0));
  Comparator #(.width(32)) comparator_1 (.a(x_rs1), .b(x_rs2), .eq(signed_BrEq), .lt(signed_Brlt));  // open: gt
  Comparator #(.width(32), .mode("unsigned")) comparator_2 (
    .a(x_rs1), .b(x_rs2), .eq(unsigned_BrEq), .lt(unsigned_Brlt));  // open: gt
  Multiplexer #(.enable("false")) multiplexer_3 (.in0(signed_BrEq), .in1(unsigned_BrEq), .out(BrEq), .sel(Brun));
  Multiplexer #(.enable("false")) multiplexer_4 (.in0(signed_Brlt), .in1(unsigned_Brlt), .out(Brlt), .sel(Brun));
  and and_9 (U_0_101, instruc_after_reg[2], not_21_out, instruc_after_reg[4], not_22_out);
  and and_10 (UJ_11011, instruc_after_reg[2], instruc_after_reg[3], not_23_out, instruc_after_reg[5], instruc_after_reg[6]);
  Multiplexer #(.width(32), .enable("false")) multiplexer_5 (
    .in0(register_2_q), .in1(x_rs1), .out(multiplexer_5_out), .sel(pc_src));
  Multiplexer #(.width(32), .enable("false")) multiplexer_6 (
    .in0(x_rs2), .in1(IMM), .out(multiplexer_6_out), .sel(op_src));
  not not_24 (not_24_out, instruc_after_reg[2]);
  not not_25 (not_25_out, instruc_after_reg[3]);
  not not_26 (not_26_out, instruc_after_reg[5]);
  not not_27 (not_27_out, instruc_after_reg[6]);
  not not_28 (not_28_out, instruc_after_reg[2]);
  not not_29 (not_29_out, instruc_after_reg[3]);
  not not_30 (not_30_out, instruc_after_reg[6]);
  BitFinder #(.width(6)) bitfinder_1 (
    .in({I_13_01, UJ_11011, U_0_101, SB_11000, S_01000, I_3_13_67}), .index(bitfinder_1_index));  // open: found
  and and_11 (i_simple_type, not_24_out, not_25_out, instruc_after_reg[4], not_26_out, not_27_out);
  and and_12 (r_type, not_28_out, not_29_out, instruc_after_reg[4], instruc_after_reg[5], not_30_out);
  not not_31 (not_31_out, instruc_after_reg[4]);
  alu Arithmetic_Logic_Unit (.A(multiplexer_5_out), .B(multiplexer_6_out), .ALUSel(alu_sel), .Result(offset));
  and and_13 (jalr_jal, instruc_after_reg[2], not_31_out, instruc_after_reg[5], instruc_after_reg[6]);
  Multiplexer #(.select(3), .width(3), .enable("false")) multiplexer_7 (
    .in0(3'b000), .in1(3'b001), .in2(3'b010), .in3(3'b011), .in4(3'b100), .in5(3'b101), .out(imm_sel),
    .sel(bitfinder_1_index));  // open: in6, in7
  Multiplexer #(.width(21), .enable("false")) multiplexer_8 (
    .in0({21{1'b0}}), .in1({21{1'b1}}), .out(I_imm[31:11]), .sel(func7[6]));
  Multiplexer #(.width(21), .enable("false")) multiplexer_9 (
    .in0({21{1'b0}}), .in1({21{1'b1}}), .out(S_imm), .sel(func7[6]));
  Multiplexer #(.width(20), .enable("false")) multiplexer_10 (
    .in0({20{1'b0}}), .in1({20{1'b1}}), .out(B_imm[31:12]), .sel(func7[6]));
  Multiplexer #(.width(12), .enable("false")) multiplexer_11 (
    .in0({12{1'b0}}), .in1({12{1'b1}}), .out(J_imm), .sel(func7[6]));
  Multiplexer #(.width(28), .enable("false")) multiplexer_12 (
    .in0({28{1'b0}}), .in1({28{1'b1}}), .out(I_SHIFT_imm), .sel(I_imm[4]));
  or or_2 (alu_result, i_simple_type, r_type, u_type_auipc);
  not not_32 (not_32_out, instruc_after_reg[2]);
  not not_33 (not_33_out, instruc_after_reg[3]);
  not not_34 (not_34_out, instruc_after_reg[4]);
  not not_35 (not_35_out, instruc_after_reg[5]);
  not not_36 (not_36_out, instruc_after_reg[6]);
  not not_37 (not_37_out, instruc_after_reg[3]);
  not not_38 (not_38_out, instruc_after_reg[6]);
  not not_39 (not_39_out, instruc_after_reg[3]);
  not not_40 (not_40_out, instruc_after_reg[5]);
  not not_41 (not_41_out, instruc_after_reg[6]);
  mem_main DMEM (
    .WriteAddr(offset), .WriteData(x_rs2), .MemRW(mem_rw),
    .ReadData({load_data[31], byte4[6:0], halfword2[7], byte3[6:0], lhu[15], byte2[6:0], lbu[7], lb[6:0]}),
    .clk(CLOCK));
  and and_14 (i_type_load, not_32_out, not_33_out, not_34_out, not_35_out, not_36_out);
  and and_15 (u_type_lui, instruc_after_reg[2], not_37_out, instruc_after_reg[4], instruc_after_reg[5], not_38_out);
  and and_16 (u_type_auipc, instruc_after_reg[2], not_39_out, instruc_after_reg[4], not_40_out, not_41_out);
  BitFinder #(.width(4)) bitfinder_2 (
    .in({u_type_lui, jalr_jal, alu_result, i_type_load}), .index(bitfinder_2_index));  // open: found
  Multiplexer #(.select(2), .width(32), .enable("false")) multiplexer_13 (
    .in0(load_result), .in1(offset), .in2(adder_2_out),
    .in3({func7[6], B_imm[10:5], I_imm[4:0], instruc_after_reg[19:15], func3, {12{1'b0}}}), .out(write_back),
    .sel(d_src));
  Multiplexer #(.select(3), .width(32), .enable("false")) multiplexer_14 (
    .in0({I_imm[31:11], B_imm[10:5], I_imm[4:0]}), .in1({S_imm, B_imm[10:1], B_imm[11]}),
    .in2({B_imm, 1'b0}),
    .in3({func7[6], B_imm[10:5], I_imm[4:0], instruc_after_reg[19:15], func3, {12{1'b0}}}),
    .in4({J_imm, instruc_after_reg[19:15], func3, I_imm[0], B_imm[10:5], I_imm[4:1], 1'b0}),
    .in5({I_SHIFT_imm, I_imm[3:0]}), .out(IMM), .sel(imm_sel));  // open: in6, in7
  not not_42 (not_42_out[1], s_type);
  Multiplexer #(.select(2), .width(2), .enable("false")) multiplexer_15 (
    .in0(2'b00), .in1(2'b01), .in2(2'b10), .in3(2'b11), .out(d_src), .sel(bitfinder_2_index));
  not not_43 (not_43_out, instruc_after_reg[2]);
  not not_44 (not_44_out, instruc_after_reg[3]);
  not not_45 (not_45_out, instruc_after_reg[4]);
  not not_46 (not_46_out, instruc_after_reg[4]);
  not not_47 (not_47_out[1], pc_used);
  not not_48 (not_48_out, instruc_after_reg[2]);
  not not_49 (not_49_out, instruc_after_reg[3]);
  not not_50 (not_50_out, instruc_after_reg[4]);
  not not_51 (not_51_out, instruc_after_reg[6]);
  not not_52 (not_52_out[1], r_type);
  and and_17 (and_17_out, not_43_out, not_44_out, not_45_out, instruc_after_reg[5], instruc_after_reg[6]);
  and and_18 (and_18_out, instruc_after_reg[2], instruc_after_reg[3], not_46_out, instruc_after_reg[5], instruc_after_reg[6]);
  and and_19 (s_type, not_48_out, not_49_out, not_50_out, instruc_after_reg[5], not_51_out);
  BitFinder #(.width(2)) bitfinder_3 (.in({not_42_out[1], s_type}), .index(bitfinder_3_index));  // open: found
  BitFinder #(.width(2)) bitfinder_4 (.in({not_47_out[1], pc_used}), .index(bitfinder_4_index));  // open: found
  Multiplexer #(.enable("false")) multiplexer_16 (.in0(1'b1), .in1(1'b0), .out(mem_rw), .sel(bitfinder_3_index));
  Comparator #(.width(3), .mode("unsigned")) comparator_3 (
    .a(func3), .b(3'b000), .eq(comparator_3_eq));  // open: gt, lt
  Comparator #(.width(3), .mode("unsigned")) comparator_4 (
    .a(func3), .b(3'b001), .eq(comparator_4_eq));  // open: gt, lt
  Comparator #(.width(3), .mode("unsigned")) comparator_5 (
    .a(func3), .b(3'b010), .eq(comparator_5_eq));  // open: gt, lt
  or or_3 (pc_used, u_type_auipc, and_17_out, and_18_out);
  Multiplexer #(.enable("false")) multiplexer_17 (.in0(1'b0), .in1(1'b1), .out(pc_src), .sel(bitfinder_4_index));
  and and_20 (is_lb, i_type_load, comparator_3_eq);
  and and_21 (is_lh, i_type_load, comparator_4_eq);
  and and_22 (is_lw, i_type_load, comparator_5_eq);
  BitFinder #(.width(2)) bitfinder_5 (.in({not_52_out[1], r_type}), .index(bitfinder_5_index));  // open: found
  Comparator #(.width(3), .mode("unsigned")) comparator_6 (
    .a(func3), .b(3'b000), .eq(comparator_6_eq));  // open: gt, lt
  Comparator #(.width(7), .mode("unsigned")) comparator_7 (
    .a({func7[6], B_imm[10:5]}), .b(7'b0000001), .eq(comparator_7_eq));  // open: gt, lt
  Comparator #(.width(3), .mode("unsigned")) comparator_8 (
    .a(func3), .b(3'b000), .eq(comparator_8_eq));  // open: gt, lt
  Comparator #(.width(7), .mode("unsigned")) comparator_9 (
    .a({func7[6], B_imm[10:5]}), .b(7'b0100000), .eq(comparator_9_eq));  // open: gt, lt
  or or_4 (or_4_out, i_simple_type, r_type);
  Comparator #(.width(3), .mode("unsigned")) comparator_10 (
    .a(func3), .b(3'b001), .eq(comparator_10_eq));  // open: gt, lt
  Comparator #(.width(7), .mode("unsigned")) comparator_11 (
    .a({func7[6], B_imm[10:5]}), .b({7{1'b0}}), .eq(comparator_11_eq));  // open: gt, lt
  Comparator #(.width(3), .mode("unsigned")) comparator_12 (
    .a(func3), .b(3'b001), .eq(comparator_12_eq));  // open: gt, lt
  Comparator #(.width(7), .mode("unsigned")) comparator_13 (
    .a({func7[6], B_imm[10:5]}), .b(7'b0000001), .eq(comparator_13_eq));  // open: gt, lt
  Multiplexer #(.enable("false")) multiplexer_18 (.in0(1'b0), .in1(1'b1), .out(op_src), .sel(bitfinder_5_index));
  Comparator #(.width(3), .mode("unsigned")) comparator_14 (
    .a(func3), .b(3'b100), .eq(comparator_14_eq));  // open: gt, lt
  Comparator #(.width(7), .mode("unsigned")) comparator_15 (
    .a({func7[6], B_imm[10:5]}), .b({7{1'b0}}), .eq(comparator_15_eq));  // open: gt, lt
  Comparator #(.width(3), .mode("unsigned")) comparator_16 (
    .a(func3), .b(3'b100), .eq(comparator_16_eq));  // open: gt, lt
  and and_23 (mul, r_type, comparator_6_eq, comparator_7_eq);
  and and_24 (sub, r_type, comparator_8_eq, comparator_9_eq);
  and and_25 (sll_slli, or_4_out, comparator_10_eq, comparator_11_eq);
  and and_26 (mulh, r_type, comparator_12_eq, comparator_13_eq);
  Comparator #(.width(3), .mode("unsigned")) comparator_17 (
    .a(func3), .b(3'b100), .eq(comparator_17_eq));  // open: gt, lt
  Comparator #(.width(3), .mode("unsigned")) comparator_18 (
    .a(func3), .b(3'b101), .eq(comparator_18_eq));  // open: gt, lt
  and and_27 (and_27_out, r_type, comparator_14_eq, comparator_15_eq);
  and and_28 (and_28_out, i_simple_type, comparator_16_eq);
  and and_29 (is_lbu, i_type_load, comparator_17_eq);
  and and_30 (is_lhu, i_type_load, comparator_18_eq);
  not not_53 (not_53_out[1], no_wb);
  or or_5 (xor_xori, and_27_out, and_28_out);
  Comparator #(.width(3), .mode("unsigned")) comparator_19 (
    .a(func3), .b(3'b101), .eq(comparator_19_eq));  // open: gt, lt
  Comparator #(.width(7), .mode("unsigned")) comparator_20 (
    .a({func7[6], B_imm[10:5]}), .b(7'b0000001), .eq(comparator_20_eq));  // open: gt, lt
  Comparator #(.width(3), .mode("unsigned")) comparator_21 (
    .a(func3), .b(3'b100), .eq(comparator_21_eq));  // open: gt, lt
  Comparator #(.width(7), .mode("unsigned")) comparator_22 (
    .a({func7[6], B_imm[10:5]}), .b(7'b0000001), .eq(comparator_22_eq));  // open: gt, lt
  Comparator #(.width(3), .mode("unsigned")) comparator_23 (
    .a(func3), .b(3'b011), .eq(comparator_23_eq));  // open: gt, lt
  Comparator #(.width(7), .mode("unsigned")) comparator_24 (
    .a({func7[6], B_imm[10:5]}), .b(7'b0000001), .eq(comparator_24_eq));  // open: gt, lt
  not not_54 (not_54_out, instruc_after_reg[2]);
  not not_55 (not_55_out, instruc_after_reg[3]);
  not not_56 (not_56_out, instruc_after_reg[4]);
  not not_57 (not_57_out, instruc_after_reg[2]);
  not not_58 (not_58_out, instruc_after_reg[3]);
  not not_59 (not_59_out, instruc_after_reg[4]);
  Comparator #(.width(3), .mode("unsigned")) comparator_25 (
    .a(func3), .b(3'b010), .eq(comparator_25_eq));  // open: gt, lt
  and and_31 (and_31_out, not_54_out, not_55_out, not_56_out, instruc_after_reg[5], instruc_after_reg[6]);
  and and_32 (divu, r_type, comparator_19_eq, comparator_20_eq);
  and and_33 (div, r_type, comparator_21_eq, comparator_22_eq);
  and and_34 (slti, i_simple_type, comparator_25_eq);
  and and_35 (mulhu, r_type, comparator_23_eq, comparator_24_eq);
  BitFinder #(.width(2)) bitfinder_6 (.in({not_53_out[1], no_wb}), .index(bitfinder_6_index));  // open: found
  or or_6 (no_wb, s_type, and_31_out);
  Multiplexer #(.enable("false")) multiplexer_19 (.in0(1'b0), .in1(1'b1), .out(reg_we), .sel(bitfinder_6_index));
  and and_36 (Brun, func3[2], not_57_out, not_58_out, not_59_out, instruc_after_reg[5], instruc_after_reg[6], func3[1]);
  Comparator #(.width(3), .mode("unsigned")) comparator_26 (
    .a(func3), .b(3'b111), .eq(comparator_26_eq));  // open: gt, lt
  Comparator #(.width(7), .mode("unsigned")) comparator_27 (
    .a({func7[6], B_imm[10:5]}), .b(7'b0000001), .eq(comparator_27_eq));  // open: gt, lt
  BitFinder #(.width(5)) bitfinder_7 (
    .in({is_lhu, is_lbu, is_lw, is_lh, is_lb}), .index(bitfinder_7_index));  // open: found
  Comparator #(.width(3), .mode("unsigned")) comparator_28 (
    .a(func3), .b(3'b111), .eq(comparator_28_eq));  // open: gt, lt
  Comparator #(.width(7), .mode("unsigned")) comparator_29 (
    .a({func7[6], B_imm[10:5]}), .b({7{1'b0}}), .eq(comparator_29_eq));  // open: gt, lt
  Comparator #(.width(3), .mode("unsigned")) comparator_30 (
    .a(func3), .b(3'b111), .eq(comparator_30_eq));  // open: gt, lt
  or or_7 (or_7_out, i_simple_type, r_type);
  Comparator #(.width(3), .mode("unsigned")) comparator_31 (
    .a(func3), .b(3'b101), .eq(comparator_31_eq));  // open: gt, lt
  Comparator #(.width(7), .mode("unsigned")) comparator_32 (
    .a({func7[6], B_imm[10:5]}), .b({7{1'b0}}), .eq(comparator_32_eq));  // open: gt, lt
  Comparator #(.width(3), .mode("unsigned")) comparator_33 (
    .a(func3), .b(3'b110), .eq(comparator_33_eq));  // open: gt, lt
  Multiplexer #(.select(3), .width(32), .enable("false")) multiplexer_20 (
    .in0(lb), .in1({lh, byte2[6:0], lbu[7], lb[6:0]}),
    .in2({load_data[31], byte4[6:0], halfword2[7], byte3[6:0], lhu[15], byte2[6:0], lbu[7], lb[6:0]}),
    .in3({{24{1'b0}}, lbu[7], lb[6:0]}), .in4({{16{1'b0}}, lhu[15], byte2[6:0], lbu[7], lb[6:0]}),
    .out(load_result), .sel(bitfinder_7_index));  // open: in5, in6, in7
  and and_37 (and_37_out, r_type, comparator_28_eq, comparator_29_eq);
  and and_38 (and_38_out, i_simple_type, comparator_30_eq);
  and and_39 (srl_srli, or_7_out, comparator_31_eq, comparator_32_eq);
  and and_40 (remu, r_type, comparator_26_eq, comparator_27_eq);
  Comparator #(.width(3), .mode("unsigned")) comparator_34 (
    .a(func3), .b(3'b110), .eq(comparator_34_eq));  // open: gt, lt
  Comparator #(.width(7), .mode("unsigned")) comparator_35 (
    .a({func7[6], B_imm[10:5]}), .b({7{1'b0}}), .eq(comparator_35_eq));  // open: gt, lt
  and and_41 (and_41_out, r_type, comparator_34_eq, comparator_35_eq);
  and and_42 (and_42_out, i_simple_type, comparator_33_eq);
  not not_60 (not_60_out, instruc_after_reg[2]);
  not not_61 (not_61_out, instruc_after_reg[3]);
  not not_62 (not_62_out, instruc_after_reg[4]);
  Comparator #(.width(1), .mode("unsigned")) comparator_36 (.a(Brlt), .b(1'b0), .eq(comparator_36_eq));  // open: gt, lt
  Comparator #(.width(1), .mode("unsigned")) comparator_37 (.a(Brun), .b(1'b1), .eq(comparator_37_eq));  // open: gt, lt
  Comparator #(.width(1), .mode("unsigned")) comparator_38 (.a(BrEq), .b(1'b1), .eq(comparator_38_eq));  // open: gt, lt
  Comparator #(.width(1), .mode("unsigned")) comparator_39 (.a(Brlt), .b(1'b0), .eq(comparator_39_eq));  // open: gt, lt
  Comparator #(.width(1), .mode("unsigned")) comparator_40 (.a(Brun), .b(1'b0), .eq(comparator_40_eq));  // open: gt, lt
  or or_8 (and_andi, and_37_out, and_38_out);
  or or_9 (or_ori, and_41_out, and_42_out);
  and and_43 (and_43_out, comparator_36_eq, comparator_37_eq);
  and and_44 (is_b_type, not_60_out, not_61_out, not_62_out, instruc_after_reg[5], instruc_after_reg[6]);
  Comparator #(.width(3), .mode("unsigned")) comparator_41 (
    .a(func3), .b(3'b111), .eq(comparator_41_eq));  // open: gt, lt
  Comparator #(.width(3), .mode("unsigned")) comparator_42 (
    .a(func3), .b(3'b000), .eq(comparator_42_eq));  // open: gt, lt
  and and_45 (and_45_out, comparator_38_eq, comparator_39_eq, comparator_40_eq);
  not not_63 (not_63_out, instruc_after_reg[4]);
  Comparator #(.width(3), .mode("unsigned")) comparator_43 (
    .a(func3), .b(3'b000), .eq(comparator_43_eq));  // open: gt, lt
  Comparator #(.width(7), .mode("unsigned")) comparator_44 (
    .a({func7[6], B_imm[10:5]}), .b({7{1'b0}}), .eq(comparator_44_eq));  // open: gt, lt
  Comparator #(.width(3), .mode("unsigned")) comparator_45 (
    .a(func3), .b(3'b000), .eq(comparator_45_eq));  // open: gt, lt
  and and_46 (bgeu, is_b_type, comparator_41_eq, and_43_out);
  and and_47 (beq, is_b_type, comparator_42_eq, and_45_out);
  not not_64 (not_64_out, instruc_after_reg[2]);
  not not_65 (not_65_out, instruc_after_reg[3]);
  Multiplexer #(.width(25), .enable("false")) multiplexer_21 (
    .in0({25{1'b0}}), .in1({25{1'b1}}), .out(lb[31:7]), .sel(lbu[7]));
  Multiplexer #(.width(25), .enable("false")) multiplexer_22 (
    .in0({25{1'b0}}), .in1({25{1'b1}}), .out(byte2[31:7]), .sel(lhu[15]));
  Multiplexer #(.width(25), .enable("false")) multiplexer_23 (
    .in0({25{1'b0}}), .in1({25{1'b1}}), .out(byte3[31:7]), .sel(halfword2[7]));
  Multiplexer #(.width(17), .enable("false")) multiplexer_24 (
    .in0({17{1'b0}}), .in1({17{1'b1}}), .out(lh), .sel(lhu[15]));
  Multiplexer #(.width(17), .enable("false")) multiplexer_25 (
    .in0({17{1'b0}}), .in1({17{1'b1}}), .out(halfword2[31:15]), .sel(load_data[31]));
  and and_48 (and_48_out, not_64_out, not_65_out, not_63_out, instruc_after_reg[5], instruc_after_reg[6]);
  and and_49 (and_49_out, r_type, comparator_43_eq, comparator_44_eq);
  and and_50 (and_50_out, i_simple_type, comparator_45_eq);
  Multiplexer #(.width(25), .enable("false")) multiplexer_26 (
    .in0({25{1'b0}}), .in1({25{1'b1}}), .out(byte4[31:7]), .sel(load_data[31]));
  or or_10 (pc_sel, bgeu, blt, beq, bltu, bne, jalr_jal);
  Comparator #(.width(1), .mode("unsigned")) comparator_46 (.a(Brlt), .b(1'b1), .eq(comparator_46_eq));  // open: gt, lt
  Comparator #(.width(1), .mode("unsigned")) comparator_47 (.a(Brun), .b(1'b0), .eq(comparator_47_eq));  // open: gt, lt
  BitFinder #(.width(15)) bitfinder_8 (
    .in({sll_slli, slti, 1'b0, srl_srli, remu, div, divu, mulh, mulhu, mul, sub, add_every, xor_xori, or_ori, and_andi}),
    .index(bitfinder_8_index));  // open: found
  Comparator #(.width(1), .mode("unsigned")) comparator_48 (.a(BrEq), .b(1'b0), .eq(comparator_48_eq));  // open: gt, lt
  or or_11 (add_every, jalr_jal, u_type_auipc, i_type_load, s_type, and_48_out, and_49_out, and_50_out);
  Comparator #(.width(3), .mode("unsigned")) comparator_49 (
    .a(func3), .b(3'b100), .eq(comparator_49_eq));  // open: gt, lt
  and and_51 (and_51_out, comparator_48_eq, comparator_46_eq, comparator_47_eq);
  Comparator #(.width(1), .mode("unsigned")) comparator_50 (.a(BrEq), .b(1'b0), .eq(comparator_50_eq));  // open: gt, lt
  Comparator #(.width(1), .mode("unsigned")) comparator_51 (.a(Brun), .b(1'b0), .eq(comparator_51_eq));  // open: gt, lt
  Multiplexer #(.select(4), .width(4), .enable("false")) multiplexer_27 (
    .in0(4'b0000), .in1(4'b0001), .in2(4'b0010), .in3(4'b0011), .in4(4'b0100), .in5(4'b0101), .in6(4'b0110),
    .in7(4'b0111), .in8(4'b1000), .in9(4'b1001), .in10(4'b1010), .in11(4'b1011), .in13(4'b1101),
    .in14(4'b1110), .out(alu_sel), .sel(bitfinder_8_index));  // open: in12, in15
  Comparator #(.width(3), .mode("unsigned")) comparator_52 (
    .a(func3), .b(3'b001), .eq(comparator_52_eq));  // open: gt, lt
  and and_52 (and_52_out, comparator_50_eq, comparator_51_eq);
  Comparator #(.width(3), .mode("unsigned")) comparator_53 (
    .a(func3), .b(3'b110), .eq(comparator_53_eq));  // open: gt, lt
  Comparator #(.width(1), .mode("unsigned")) comparator_54 (.a(BrEq), .b(1'b0), .eq(comparator_54_eq));  // open: gt, lt
  Comparator #(.width(1), .mode("unsigned")) comparator_55 (.a(Brlt), .b(1'b1), .eq(comparator_55_eq));  // open: gt, lt
  Comparator #(.width(1), .mode("unsigned")) comparator_56 (.a(Brun), .b(1'b1), .eq(comparator_56_eq));  // open: gt, lt
  and and_53 (blt, is_b_type, comparator_49_eq, and_51_out);
  and and_54 (bne, is_b_type, comparator_52_eq, and_52_out);
  and and_55 (and_55_out, comparator_54_eq, comparator_55_eq, comparator_56_eq);
  Multiplexer #(.select(2), .width(32), .enable("false")) multiplexer_28 (
    .in0(byte1), .in1(byte2), .in2(byte3), .in3(byte4), .sel(offset[1:0]));  // open: out
  Multiplexer #(.width(32), .enable("false")) multiplexer_29 (
    .in0(halfword1), .in1({halfword2[31:15], byte4[6:0], halfword2[7], byte3[6:0]}), .sel(offset[0]));  // open: out
  and and_56 (bltu, is_b_type, comparator_53_eq, and_55_out);
  Multiplexer #(.select(2), .width(32), .enable("false")) multiplexer_30 (
    .in0(ubyte1), .in1({{24{1'b0}}, lhu[15], byte2[6:0]}), .in2({{24{1'b0}}, halfword2[7], byte3[6:0]}),
    .in3({{24{1'b0}}, load_data[31], byte4[6:0]}), .sel(offset[1:0]));  // open: out
  Multiplexer #(.width(32), .enable("false")) multiplexer_31 (
    .in0({{16{1'b0}}, load_data[31], byte4[6:0], halfword2[7], byte3[6:0]}), .in1(uhalfword2), .sel(offset[0]));  // open: out

  // Other names for the same wires on the sheet: instruc_after_reg (some bits) = {func7[6], B_imm[10:5], I_imm[4:0], func3, B_imm[4:1], B_imm[11]};
  //   RD[4:0] = {B_imm[4:1], B_imm[11]}; S_imm[10:0] = {B_imm[10:1], B_imm[11]}; clk = CLOCK;
  //   fetch_addr[31:0] = FETCH_ADDRESS; I_SHIFT_imm[3:0] = I_imm[3:0];
  //   J_imm[19:1] = {instruc_after_reg[19:15], func3, I_imm[0], B_imm[10:5], I_imm[4:1]}; RS2[4:0] = I_imm[4:0];
  //   U_imm[31:12] = {func7[6], B_imm[10:5], I_imm[4:0], instruc_after_reg[19:15], func3};
  //   Opcode[6:0] = instruc_after_reg[6:0]; func7[5:0] = B_imm[10:5]; I_imm[10:5] = B_imm[10:5];
  //   RS1[4:0] = instruc_after_reg[19:15]; lbu[6:0] = lb[6:0]; lh[14:0] = {byte2[6:0], lbu[7], lb[6:0]};
  //   lhu[14:0] = {byte2[6:0], lbu[7], lb[6:0]};
  //   load_data[30:0] = {byte4[6:0], halfword2[7], byte3[6:0], lhu[15], byte2[6:0], lbu[7], lb[6:0]};
  //   lw[31:0] = {load_data[31], byte4[6:0], halfword2[7], byte3[6:0], lhu[15], byte2[6:0], lbu[7], lb[6:0]};
  //   ubyte2[7:0] = {lhu[15], byte2[6:0]}; halfword2 (some bits) = {byte4[6:0], byte3[6:0]};
  //   ubyte3[7:0] = {halfword2[7], byte3[6:0]};
  //   uhalfword1[15:0] = {load_data[31], byte4[6:0], halfword2[7], byte3[6:0]};
  //   ubyte4[7:0] = {load_data[31], byte4[6:0]}

  // Notes on the sheet:
  //   Output
  //   GET THE REGISTER
  //   instruc_after_reg
  //   decode_1
  //   Inputs/Outputs from run.circ. DO NOT MOVE THESE.
  //   Inputs
  //   IMM_CONTROL_LOGIC
  //   It is OK to move the PC, RegFile, ALU, and MEM to wherever is most convenient for you when constructing your CPU, and to delete this text
  //   comp logic
  //   Inputs/Outputs from run.circ. DO NOT MOVE THESE.
  //   I_TYPE
  //   S_TYPE
  //   B_TYPE
  //   U_TYPE
  //   J_TYPE
  //   I_SHIFT_TYPE
  //   IMM_SEL
  //   imm_gen
  //   d_src
  //   sel_imm
  //   mem_rw
  //   op_src
  //   pc_src
  //   alu_sel
  //   reg_we
  //   Brun
  //   pc_sel
endmodule
